# Fritzing sketch Raj (saved by Fritzing 0.9.3b)
breadboards: 1

parts:
  U1 = ESP8266 NodeMCU LoLin module
  M2 = MAX30102
  Mod1 = Full Size SD Card Module

nets:
  N1: U1.D1, M2.SCL
  N2: U1.D2, M2.SDA
  3V3: U1.3V3, M2.VIN, Mod1.pin_3, Mod1.pin_4
  GND: U1.GND, M2.GND, Mod1.pin_1

custom parts:
  ESP8266 NodeMCU LoLin module: ESP8266 based NodeMCU
  MAX30102: Oximeter module using the MAX30102 chip. You may wish to read (and check your module) this post on power problems with these modules: https://reedpaper.wordpress.com/2018/08/22/pulse-oximeter-max30100-max30102-how-to-fix-wrong-board/ . As usual, if you want the mounting holes in pcb, you need to drag a hole over the pad in silkscreen to actually drill the hole (by default they are not drilled)
  Full Size SD Card Module: SD Card Module Slot Socket Reader For Arduino ARM MCU
